# Fritzing sketch astavel (saved by Fritzing 1.0.5)
circuit board: 8.46667cm x 5.64444cm

parts:
  R2 = Resistor [tolerance=±5% power=0.25W resistance=220 package=THT]
  R3 = Resistor [tolerance=±5% power=0.25W resistance=220 package=THT]
  C1 = Electrolytic Capacitor [capacitance=1µF voltage=35V package="100 mil [THT, electrolytic]"]
  Q1 = NPN-Transistor [package="TO92 [THT]"]
  C2 = Electrolytic Capacitor [capacitance=1µF voltage=35V package="100 mil [THT, electrolytic]"]
  Q2 = NPN-Transistor [package="TO92 [THT]"]
  LED2 = LED - 5mm [color="Red (633nm)" current=0.030A package="5 mm [THT]"]
  LED1 = LED - 5mm [color="Red (633nm)" current=0.030A package="5 mm [THT]"]
  R4 = Resistor [tolerance=±5% power=0.25W resistance=220 package=THT]
  R1 = Resistor [tolerance=±5% power=0.25W resistance=220 package=THT]

nets:
  N1: R2.Pin_0, R3.Pin_0, R4.Pin_0, R1.Pin_0
  N2: R2.Pin_1, C1.-, Q1.B
  N3: R3.Pin_1, C2.-, Q2.B
  N4: C1.+, Q2.C, LED1.cathode
  N5: Q1.E, Q2.E
  N6: Q1.C, C2.+, LED2.cathode
  N7: LED2.anode, R4.Pin_1
  N8: LED1.anode, R1.Pin_1
